// Logisim project InstructionDecoder.circ as structural Verilog: 4 circuits, main circuit InstructionDecoder
module InstructionDecoder (
  input  [31:0] instruction,
  output add,
  output mul,
  output sub,
  output mulh,
  output [4:0] rd,
  output op_sll,
  output mulsu,
  output [4:0] rs1,
  output op_slt,
  output [4:0] rs2,
  output mulu,
  output op_sltu,
  output div,
  output op_xor,
  output divu,
  output op_slr,
  output op_rem,
  output op_sra,
  output remu,
  output op_or,
  output op_and,
  output addi,
  output slli,
  output [31:0] imm,
  output slti,
  output sltiu,
  output xori,
  output srli,
  output srai,
  output ori,
  output andi,
  output lb,
  output lh,
  output lw,
  output lbu,
  output lhu,
  output sb,
  output sh,
  output sw,
  output beq,
  output bne,
  output blt,
  output bge,
  output bltu,
  output bgeu,
  output jal,
  output jalr,
  output lui,
  output auipc,
  output ecall,
  output ebreak
);

  wire B, I, J, opcodedecoder_1_r, S, U;

  swirl swirl_1 (
    .funct7(instruction[31:25]), .rs2(instruction[24:20]), .rs1(instruction[19:15]),
    .funct3(instruction[14:12]), .rd(instruction[11:7]), .B(B), .I(I), .S(S), .J(J), .U(U), .imm(imm));
  OpcodeDecoder opcodedecoder_1 (
    .opcode(instruction[6:0]), .funct3(instruction[14:12]), .funct7(instruction[31:25]),
    .rs2(instruction[24:20]), .jalr(jalr), .ecall(ecall), .ebreak(ebreak), .J(J), .jal(jal), .lui(lui),
    .auipc(auipc), .S(S), .B(B), .U(U), .sb(sb), .sh(sh), .sw(sw), .beq(beq), .bne(bne), .blt(blt),
    .bge(bge), .bltu(bltu), .bgeu(bgeu), .R(opcodedecoder_1_r), .sub(sub), .op_sll(op_sll), .op_slt(op_slt),
    .op_sltu(op_sltu), .op_xor(op_xor), .op_slr(op_slr), .op_sra(op_sra), .op_or(op_or), .op_and(op_and),
    .addi(addi), .slli(slli), .slti(slti), .sltiu(sltiu), .xori(xori), .srli(srli), .srai(srai), .ori(ori),
    .andi(andi), .add(add), .lb(lb), .lh(lh), .lw(lw), .lbu(lbu), .lhu(lhu), .I(I), .mulh(mulh),
    .mulsu(mulsu), .mulu(mulu), .div(div), .divu(divu), .op_rem(op_rem), .remu(remu), .mul(mul));
  // NoConnect on opcodedecoder_1_r

  assign rd = instruction[11:7];
  assign rs1 = instruction[19:15];
  assign rs2 = instruction[24:20];

  // Other names for the same wires on the sheet: opcode[6:0] = instruction[6:0]; funct3[2:0] = instruction[14:12];
  //   funct7[6:0] = instruction[31:25]
endmodule

module swirl (
  input  [6:0] funct7,
  input  [4:0] rs2,
  input  [4:0] rs1,
  input  [2:0] funct3,
  input  [4:0] rd,
  input  B,
  input  I,
  input  S,
  input  J,
  input  U,
  output [31:0] imm
);

  wire undriven;
  wire [2:0] priority_encoder_1_out;
  wire [31:0] B_t, I_t, J_t, S_t;

  assign I_t = {{20{funct7[6]}}, {funct7, rs2}};  // Bit_Extender bit_extender_1
  // NoConnect on nothing
  assign B_t = {{19{funct7[6]}}, {funct7[6], rd[0], funct7[5:0], rd[4:1], 1'b0}};  // Bit_Extender bit_extender_2
  Multiplexer #(.select(3), .width(32)) multiplexer_1 (
    .in0({32{1'b0}}), .in1(B_t), .in2(I_t), .in3(S_t), .in4(J_t),
    .in5({funct7, rs2, rs1, funct3, {12{1'b0}}}), .in6({32{1'b0}}), .in7({32{1'b0}}), .out(imm),
    .sel(priority_encoder_1_out));
  // NoConnect on nothing
  Priority_Encoder priority_encoder_1 (
    .in0(1'b0), .in1(B), .in2(I), .in3(S), .in4(J), .in5(U), .in6(1'b0), .in7(1'b0),
    .out(priority_encoder_1_out), .en_in(undriven));
  // NoConnect on undriven
  assign S_t = {{20{funct7[6]}}, {funct7, rd}};  // Bit_Extender bit_extender_3
  assign J_t = {{11{funct7[6]}}, {funct7[6], rs1, funct3, rs2[0], funct7[5:0], rs2[4:1], 1'b0}};  // Bit_Extender bit_extender_4

  // Other names for the same wires on the sheet: U_t[31:12] = {funct7, rs2, rs1, funct3};
  //   Uimm[19:0] = {funct7, rs2, rs1, funct3}

  // Notes on the sheet:
  //   imm: pull=down
  //   I
  //   B
  //   S
  //   J
endmodule

module OpcodeDecoder (
  input  [6:0] opcode,
  input  [2:0] funct3,
  input  [6:0] funct7,
  input  [4:0] rs2,
  output add,
  output mul,
  output sub,
  output mulh,
  output R,
  output op_sll,
  output mulsu,
  output op_slt,
  output mulu,
  output sb,
  output op_sltu,
  output div,
  output S,
  output sh,
  output op_xor,
  output divu,
  output sw,
  output op_slr,
  output op_rem,
  output op_sra,
  output remu,
  output op_or,
  output op_and,
  output beq,
  output bne,
  output B,
  output blt,
  output bge,
  output bltu,
  output addi,
  output bgeu,
  output slli,
  output jalr,
  output slti,
  output J,
  output jal,
  output sltiu,
  output xori,
  output ecall,
  output srli,
  output ebreak,
  output srai,
  output lui,
  output ori,
  output U,
  output andi,
  output auipc,
  output lb,
  output lh,
  output I,
  output lw,
  output lbu,
  output lhu
);

  wire and_14_out, compare7bits_4_equal, compare7bits_5_equal, compare7bits_6_equal, demultiplexer_1_out0,
       demultiplexer_1_out1, demultiplexer_1_out2, demultiplexer_1_out3, demultiplexer_1_out4,
       demultiplexer_1_out5, demultiplexer_1_out6, demultiplexer_1_out7, demultiplexer_2_out1,
       demultiplexer_2_out5, demultiplexer_3_out3, demultiplexer_3_out6, demultiplexer_3_out7,
       demultiplexer_6_out3, demultiplexer_6_out4, demultiplexer_6_out5, demultiplexer_6_out6,
       demultiplexer_6_out7, demultiplexer_7_out2, demultiplexer_7_out3, I1, I2, I4;

  compare7bits compare7bits_1 (.A(7'b0110011), .B(opcode), .equal(R));
  compare7bits compare7bits_2 (.A(opcode), .B(7'b0010011), .equal(I1));
  compare7bits compare7bits_3 (.A(opcode), .B(7'b0000011), .equal(I2));
  Demultiplexer #(.select(3)) demultiplexer_1 (
    .out0(demultiplexer_1_out0), .out1(demultiplexer_1_out1), .out2(demultiplexer_1_out2),
    .out3(demultiplexer_1_out3), .out4(demultiplexer_1_out4), .out5(demultiplexer_1_out5),
    .out6(demultiplexer_1_out6), .out7(demultiplexer_1_out7), .in(R), .sel(funct3));
  compare7bits compare7bits_4 (.A({7{1'b0}}), .B(funct7), .equal(compare7bits_4_equal));
  compare7bits compare7bits_5 (.A(funct7), .B(7'b0100000), .equal(compare7bits_5_equal));
  Demultiplexer #(.select(3)) demultiplexer_2 (
    .out0(addi), .out1(demultiplexer_2_out1), .out2(slti), .out3(sltiu), .out4(xori),
    .out5(demultiplexer_2_out5), .out6(ori), .out7(andi), .in(I1), .sel(funct3));
  // NoConnect on demultiplexer_3_out3
  Demultiplexer #(.select(3)) demultiplexer_3 (
    .out0(lb), .out1(lh), .out2(lw), .out3(demultiplexer_3_out3), .out4(lbu), .out5(lhu),
    .out6(demultiplexer_3_out6), .out7(demultiplexer_3_out7), .in(I2), .sel(funct3));
  // NoConnect on demultiplexer_3_out6
  // NoConnect on demultiplexer_3_out7
  and and_1 (add, demultiplexer_1_out0, compare7bits_4_equal);
  and and_2 (sub, demultiplexer_1_out0, compare7bits_5_equal);
  and and_3 (op_sll, demultiplexer_1_out1, compare7bits_4_equal);
  and and_4 (op_slt, demultiplexer_1_out2, compare7bits_4_equal);
  and and_5 (op_sltu, demultiplexer_1_out3, compare7bits_4_equal);
  and and_6 (op_xor, demultiplexer_1_out4, compare7bits_4_equal);
  and and_7 (op_slr, demultiplexer_1_out5, compare7bits_4_equal);
  and and_8 (op_sra, demultiplexer_1_out5, compare7bits_5_equal);
  and and_9 (op_or, demultiplexer_1_out6, compare7bits_4_equal);
  and and_10 (op_and, demultiplexer_1_out7, compare7bits_4_equal);
  and and_11 (slli, compare7bits_4_equal, demultiplexer_2_out1);
  and and_12 (srli, demultiplexer_2_out5, compare7bits_4_equal);
  and and_13 (srai, demultiplexer_2_out5, compare7bits_5_equal);
  and and_14 (and_14_out, R, compare7bits_6_equal);
  Demultiplexer #(.select(3)) demultiplexer_4 (
    .out0(mul), .out1(mulh), .out2(mulsu), .out3(mulu), .out4(div), .out5(divu), .out6(op_rem), .out7(remu),
    .in(and_14_out), .sel(funct3));
  compare7bits compare7bits_6 (.A(7'b0000001), .B(funct7), .equal(compare7bits_6_equal));
  compare7bits compare7bits_7 (.A(7'b1100111), .B(opcode), .equal(jalr));
  Demultiplexer demultiplexer_5 (.out0(ecall), .out1(ebreak), .in(I4), .sel(rs2[0]));
  compare7bits compare7bits_8 (.A(7'b1110011), .B(opcode), .equal(I4));
  or or_1 (I, I1, I2, jalr, I4);
  compare7bits compare7bits_9 (.A(opcode), .B(7'b0100011), .equal(S));
  compare7bits compare7bits_10 (.A(7'b1100011), .B(opcode), .equal(B));
  compare7bits compare7bits_11 (.A(7'b1101111), .B(opcode), .equal(J));
  compare7bits compare7bits_12 (.A(7'b0110111), .B(opcode), .equal(lui));
  compare7bits compare7bits_13 (.A(7'b0010111), .B(opcode), .equal(auipc));
  Demultiplexer #(.select(3)) demultiplexer_6 (
    .out0(sb), .out1(sh), .out2(sw), .out3(demultiplexer_6_out3), .out4(demultiplexer_6_out4),
    .out5(demultiplexer_6_out5), .out6(demultiplexer_6_out6), .out7(demultiplexer_6_out7), .in(S),
    .sel(funct3));
  Demultiplexer #(.select(3)) demultiplexer_7 (
    .out0(beq), .out1(bne), .out2(demultiplexer_7_out2), .out3(demultiplexer_7_out3), .out4(blt), .out5(bge),
    .out6(bltu), .out7(bgeu), .in(B), .sel(funct3));
  // NoConnect on demultiplexer_6_out3
  // NoConnect on demultiplexer_6_out4
  // NoConnect on demultiplexer_6_out5
  // NoConnect on demultiplexer_6_out6
  // NoConnect on demultiplexer_6_out7
  // NoConnect on demultiplexer_7_out2
  // NoConnect on demultiplexer_7_out3
  or or_2 (U, lui, auipc);

  assign jal = J;

  // Other names for the same wires on the sheet: I3 = jalr
endmodule

module compare7bits (
  input  [6:0] A,
  input  [6:0] B,
  output equal
);

  wire [6:0] xnor_1_out;

  assign xnor_1_out = ~(A ^ B);  // XNOR_Gate xnor_1, 7 bits wide
  and and_1 (equal, xnor_1_out[0], xnor_1_out[1], xnor_1_out[2], xnor_1_out[3], xnor_1_out[4], xnor_1_out[5], xnor_1_out[6]);
endmodule
